// Digital circuit jogo_matriz.dig as structural Verilog
module jogo_matriz (
  input  clk,
  output [6:0] db_estado,
  output [6:0] db_nivel,
  output [6:0] db_botoes,
  output [7:0] linha,
  output [7:0] coluna,
  output [4:0] s_estado
);

  wire Jogar_out, rst_out, u_jogo_desafio_memoria_ganhou;
  wire [7:0] botao_0_out;

  Button botao_0 (.out(botao_0_out[0]));
  Button botao_1 (.out(botao_0_out[1]));
  Button botao_2 (.out(botao_0_out[2]));
  Button botao_3 (.out(botao_0_out[3]));
  Button botao_4 (.out(botao_0_out[4]));
  Button botao_5 (.out(botao_0_out[5]));
  Button botao_6 (.out(botao_0_out[6]));
  Button botao_7 (.out(botao_0_out[7]));
  Button rst (.out(rst_out));
  Button Jogar (.out(Jogar_out));
  jogo_desafio_memoria #(.applicationType("IVERILOG")) u_jogo_desafio_memoria (
    .clock(clk), .reset(rst_out), .jogar(Jogar_out), .botoes(botao_0_out), .colunas(coluna), .linhas(linha),
    .ganhou(u_jogo_desafio_memoria_ganhou), .db_estado(db_estado), .db_nivel(db_nivel),
    .db_botoes(db_botoes), .estados(s_estado));
  LED Ganhou (.in(u_jogo_desafio_memoria_ganhou));
  // PolarityAwareLED polarityawareled_1: pin names not known; wires that end beside it: coluna[0], linha[0], coluna[0]
  // PolarityAwareLED polarityawareled_2: pin names not known; wires that end beside it: linha[1], coluna[0]
  // PolarityAwareLED polarityawareled_3: pin names not known; wires that end beside it: linha[2], coluna[0]
  // PolarityAwareLED polarityawareled_4: pin names not known; wires that end beside it: linha[3], coluna[0]
  // PolarityAwareLED polarityawareled_5: pin names not known; wires that end beside it: linha[4], coluna[0]
  // PolarityAwareLED polarityawareled_6: pin names not known; wires that end beside it: linha[5], coluna[0]
  // PolarityAwareLED polarityawareled_7: pin names not known; wires that end beside it: linha[6], coluna[0]
  // PolarityAwareLED polarityawareled_8: pin names not known; wires that end beside it: linha[7]
  // PolarityAwareLED polarityawareled_9: pin names not known; wires that end beside it: coluna[1], linha[0], coluna[1]
  // PolarityAwareLED polarityawareled_10: pin names not known; wires that end beside it: linha[1], coluna[1]
  // PolarityAwareLED polarityawareled_11: pin names not known; wires that end beside it: linha[2], coluna[1]
  // PolarityAwareLED polarityawareled_12: pin names not known; wires that end beside it: linha[3], coluna[1]
  // PolarityAwareLED polarityawareled_13: pin names not known; wires that end beside it: linha[4], coluna[1]
  // PolarityAwareLED polarityawareled_14: pin names not known; wires that end beside it: linha[5], coluna[1]
  // PolarityAwareLED polarityawareled_15: pin names not known; wires that end beside it: linha[6], coluna[1]
  // PolarityAwareLED polarityawareled_16: pin names not known; wires that end beside it: linha[7]
  // PolarityAwareLED polarityawareled_17: pin names not known; wires that end beside it: coluna[2], linha[0], coluna[2]
  // PolarityAwareLED polarityawareled_18: pin names not known; wires that end beside it: linha[1], coluna[2]
  // PolarityAwareLED polarityawareled_19: pin names not known; wires that end beside it: linha[2], coluna[2]
  // PolarityAwareLED polarityawareled_20: pin names not known; wires that end beside it: linha[3], coluna[2]
  // PolarityAwareLED polarityawareled_21: pin names not known; wires that end beside it: linha[4], coluna[2]
  // PolarityAwareLED polarityawareled_22: pin names not known; wires that end beside it: linha[5], coluna[2]
  // PolarityAwareLED polarityawareled_23: pin names not known; wires that end beside it: linha[6], coluna[2]
  // PolarityAwareLED polarityawareled_24: pin names not known; wires that end beside it: linha[7]
  // PolarityAwareLED polarityawareled_25: pin names not known; wires that end beside it: coluna[3], linha[0], coluna[3]
  // PolarityAwareLED polarityawareled_26: pin names not known; wires that end beside it: linha[1], coluna[3]
  // PolarityAwareLED polarityawareled_27: pin names not known; wires that end beside it: linha[2], coluna[3]
  // PolarityAwareLED polarityawareled_28: pin names not known; wires that end beside it: linha[3], coluna[3]
  // PolarityAwareLED polarityawareled_29: pin names not known; wires that end beside it: linha[4], coluna[3]
  // PolarityAwareLED polarityawareled_30: pin names not known; wires that end beside it: linha[5], coluna[3]
  // PolarityAwareLED polarityawareled_31: pin names not known; wires that end beside it: linha[6], coluna[3]
  // PolarityAwareLED polarityawareled_32: pin names not known; wires that end beside it: linha[7]
  // PolarityAwareLED polarityawareled_33: pin names not known; wires that end beside it: coluna[4], linha[0], coluna[4]
  // PolarityAwareLED polarityawareled_34: pin names not known; wires that end beside it: linha[1], coluna[4]
  // PolarityAwareLED polarityawareled_35: pin names not known; wires that end beside it: linha[2], coluna[4]
  // PolarityAwareLED polarityawareled_36: pin names not known; wires that end beside it: linha[3], coluna[4]
  // PolarityAwareLED polarityawareled_37: pin names not known; wires that end beside it: linha[4], coluna[4]
  // PolarityAwareLED polarityawareled_38: pin names not known; wires that end beside it: linha[5], coluna[4]
  // PolarityAwareLED polarityawareled_39: pin names not known; wires that end beside it: linha[6], coluna[4]
  // PolarityAwareLED polarityawareled_40: pin names not known; wires that end beside it: linha[7]
  // PolarityAwareLED polarityawareled_41: pin names not known; wires that end beside it: coluna[5], linha[0], coluna[5]
  // PolarityAwareLED polarityawareled_42: pin names not known; wires that end beside it: linha[1], coluna[5]
  // PolarityAwareLED polarityawareled_43: pin names not known; wires that end beside it: linha[2], coluna[5]
  // PolarityAwareLED polarityawareled_44: pin names not known; wires that end beside it: linha[3], coluna[5]
  // PolarityAwareLED polarityawareled_45: pin names not known; wires that end beside it: linha[4], coluna[5]
  // PolarityAwareLED polarityawareled_46: pin names not known; wires that end beside it: linha[5], coluna[5]
  // PolarityAwareLED polarityawareled_47: pin names not known; wires that end beside it: linha[6], coluna[5]
  // PolarityAwareLED polarityawareled_48: pin names not known; wires that end beside it: linha[7]
  // PolarityAwareLED polarityawareled_49: pin names not known; wires that end beside it: coluna[6], linha[0], coluna[6]
  // PolarityAwareLED polarityawareled_50: pin names not known; wires that end beside it: linha[1], coluna[6]
  // PolarityAwareLED polarityawareled_51: pin names not known; wires that end beside it: linha[2], coluna[6]
  // PolarityAwareLED polarityawareled_52: pin names not known; wires that end beside it: linha[3], coluna[6]
  // PolarityAwareLED polarityawareled_53: pin names not known; wires that end beside it: linha[4], coluna[6]
  // PolarityAwareLED polarityawareled_54: pin names not known; wires that end beside it: linha[5], coluna[6]
  // PolarityAwareLED polarityawareled_55: pin names not known; wires that end beside it: linha[6], coluna[6]
  // PolarityAwareLED polarityawareled_56: pin names not known; wires that end beside it: linha[7]
  // PolarityAwareLED polarityawareled_57: pin names not known; wires that end beside it: coluna[7], linha[0], coluna[7]
  // PolarityAwareLED polarityawareled_58: pin names not known; wires that end beside it: linha[1], coluna[7]
  // PolarityAwareLED polarityawareled_59: pin names not known; wires that end beside it: linha[2], coluna[7]
  // PolarityAwareLED polarityawareled_60: pin names not known; wires that end beside it: linha[3], coluna[7]
  // PolarityAwareLED polarityawareled_61: pin names not known; wires that end beside it: linha[4], coluna[7]
  // PolarityAwareLED polarityawareled_62: pin names not known; wires that end beside it: linha[5], coluna[7]
  // PolarityAwareLED polarityawareled_63: pin names not known; wires that end beside it: linha[6], coluna[7]
  // PolarityAwareLED polarityawareled_64: pin names not known; wires that end beside it: linha[7]

  // Notes on the sheet:
  //   clk: Hz: 500
endmodule

/* Code of jogo_desafio_memoria:
// -------------------------------------------
// Modulo principal que conecta a UC com o FD
// -------------------------------------------

module jogo_desafio_memoria (
    input  clock,
    input  reset,
    input  jogar,
    input  [7:0] botoes,
    output [7:0] colunas,
    output [7:0] linhas,
    output ganhou,
    output [6:0] db_estado,
    output [6:0] db_nivel,
    output [6:0] db_botoes,
    output [4:0] estados
);

    // Sinais internos para interligacao dos componentes
    wire s_nivel_concluido;
    wire s_nivelIgualUltimoNivel;
    wire s_nivelMenorOuIgualUltimoNivel;
    wire s_contaN;
    wire s_zeraN;
    wire s_zeraM;
    wire s_contaT;
    wire s_zeraT;
    wire s_contaP;
    wire s_zeraP;
    wire s_ganhou;
    wire s_passou_nivel;
    wire s_fimT;
    wire s_fimP;
    wire [4:0] s_estado;
    wire [2:0] s_nivel;
    wire [7:0] s_botoes;

    // Unidade de controle
    unidade_controle unidade_controle (
        .clock                        ( clock ),    
        .reset                        ( reset ),
        .iniciar                      ( jogar ),
        .fimT                         ( s_fimT ),
        .fimP                         ( s_fimP ),
        .nivel_concluido              ( s_nivel_concluido ),
        .nivelIgualUltimoNivel        ( s_nivelIgualUltimoNivel ),
        .nivelMenorOuIgualUltimoNivel ( s_nivelMenorOuIgualUltimoNivel ),
        .ganhou                       ( s_ganhou ),
        .passou_nivel                 ( s_passou_nivel ),
        .contaN                       ( s_contaN ),
        .zeraN                        ( s_zeraN ),
        .contaT                       ( s_contaT ),
        .zeraT                        ( s_zeraT ), 
        .contaP                       ( s_contaP ),
        .zeraP                        ( s_zeraP ), 
        .zeraM                        ( s_zeraM ),
        .db_estado                    ( s_estado )
    );

    // Fluxo de dados
    fluxo_dados fluxo_dados (
        .clock                        ( clock ),        
        .contaN                       ( s_contaN ),  
        .zeraN                        ( s_zeraN ), 
        .contaT                       ( s_contaT ),
        .zeraT                        ( s_zeraT ), 
        .contaP                       ( s_contaP ),
        .zeraP                        ( s_zeraP ),   
        .zeraM                        ( s_zeraM ),   
        .ganhou                       ( s_ganhou ),
        .passou_nivel                 ( s_passou_nivel ),
        .botoes                       ( botoes ),
        .fimT                         ( s_fimT ),
        .fimP                         ( s_fimP ),
        .nivel_concluido              ( s_nivel_concluido ),
        .colunas                      ( colunas ),
        .linhas                       ( linhas ),
        .nivelIgualUltimoNivel        ( s_nivelIgualUltimoNivel ),
        .nivelMenorOuIgualUltimoNivel ( s_nivelMenorOuIgualUltimoNivel ),
        .db_nivel                     ( s_nivel ),
        .db_botoes                    ( s_botoes )
    );

    // Display dos niveis
    hexa7seg_ent3bit HEX0 (
        .hexa    ( s_nivel ), 
        .display ( db_nivel )
    );

    // Display dos botões
    hexa7seg_ent8bit HEX1 (
        .hexa    ( s_botoes ), 
        .display ( db_botoes )
    );

    // Display dos estados
    hexa7seg_mod HEX2 (
        .hexa    ( s_estado ),
        .display ( db_estado )
    );

    // Saida depuração
    assign ganhou = s_ganhou;
    assign estados = s_estado;

endmodule

/*
 * ------------------------------------------------------------------
 *  Arquivo   : fluxo_dados.v
 *  Projeto   : Projeto de jogo com matriz de leds
 * ------------------------------------------------------------------
 *  Descricao : Fluxo de dados do projeto
 * ------------------------------------------------------------------
 * /


module fluxo_dados (
  input  clock,
  input  contaN,  
  input  zeraN, 
  input  contaT,
  input  zeraT, 
  input  contaP,
  input  zeraP,   
  input  zeraM, 
  input  ganhou,
  input  passou_nivel,
  input  [7:0] botoes,
  output fimT,
  output fimP,
  output nivel_concluido,
  output [7:0] colunas,
  output [7:0] linhas,
  output nivelIgualUltimoNivel,
  output nivelMenorOuIgualUltimoNivel,
  output [2:0] db_nivel,
  output [7:0] db_botoes
);

  // sinais internos para interligacao dos componentes
  wire [2:0] s_nivel;
  wire [7:0] s_botoes;
  wire [2:0] s_indice;
  wire [7:0] s_col_reg;
  wire [7:0] s_col_mat;
  wire s_sinal;
  wire s_reg_enable;

  // contador_163 nivel
  contador_163 contador_nivel (
    .clock ( clock ),
    .clr   ( ~zeraN ),
    .ld    ( 1'b1 ),
    .ent   ( 1'b1 ),
    .enp   ( contaN ),
    .D     ( 3'b000 ),
    .Q     ( s_nivel ),
    .rco   (  )          // n precisa por enquanto
  );

  // Matriz de leds
  matriz_leds matriz (
    .clk             ( clock ),              
    .rst             ( zeraM ),              
    .botoes          ( s_botoes ),     
    .nivel           ( s_nivel ),      
    .nivel_concluido ( nivel_concluido ), 
    .colunas         ( s_col_mat ),   
    .linhas          ( linhas ),
    .indice          ( s_indice )   
  );

  // comparador_85 nivel
  comparador_85 comparador_nivel (
    .A    ( s_nivel ),
    .B    ( 3'b100 ),
    .ALBi ( 1'b0 ),
    .AGBi ( 1'b0 ),
    .AEBi ( 1'b1 ),
    .ALBo (  ),                        // Não utilizado
    .AGBo ( nivelMenorOuIgualUltimoNivel ),                    
    .AEBo ( nivelIgualUltimoNivel )
  );

  // edge detector global
  edge_detector_global edging_geral (
    .clock         ( clock ),
    .reset         ( zeraM ),
    .botoes        ( botoes ),
    .edge_detected ( s_botoes )
  );

  // edge detector
  edge_detector edging (
    .clock( clock ),
    .reset( zeraM ),
    .sinal( s_sinal ),
    .pulso( s_reg_enable )
  );

  // registrador do db_botões
  registrador_8 reg_botoes (
    .clock         ( clock ),
    .clear         ( zeraM ),
    .enable        ( s_reg_enable ),
    .D             ( botoes ),
    .Q             ( db_botoes )
  );

  // registrador para o desenho de vitória e todos acesos
  reg_8x8 reg_desenho (
    .clock       ( clock ),
    .reset       ( zeraM ),
    .indice      ( s_indice ),
    .vitoria     ( ganhou ),
    .coluna_sel  ( s_col_reg )
  );

  // timer da piscagem
  contador_m #(500, 9) timer_piscagem (             
    .clock   ( clock ),
    .zera_as ( 1'b0 ),
    .zera_s  ( zeraT ),
    .conta   ( contaT ),
    .Q       (  ), 
    .fim     ( fimT ),
    .meio    (  )
  );

  // contador da piscagem
  contador_m #(3, 2) contador_piscagem ( 
    .clock   ( clock ),
    .zera_as ( 1'b0 ),
    .zera_s  ( zeraP ),
    .conta   ( contaP ), 
    .Q       (  ),
    .fim     ( fimP ),
    .meio    (  )
  );


  // entrada edger
  assign s_sinal = |botoes;

  // saida da coluna
  assign colunas = passou_nivel ? s_col_reg : s_col_mat;

  // saida de depuracao
  assign db_nivel  = s_nivel;

endmodule

//------------------------------------------------------------------
// Arquivo   : exp3_unidade_controle_desafio.v
// Projeto   : Experiencia 3 - Projeto de uma Unidade de Controle
//------------------------------------------------------------------
// Descricao : Unidade de controle
//
// usar este codigo como template (modelo) para codificar 
// máquinas de estado de unidades de controle            
//------------------------------------------------------------------
// Revisoes  :
//     Data        Versao  Autor             Descricao
//     14/01/2024  1.0     Edson Midorikawa  versao inicial
//     12/01/2025  1.1     Edson Midorikawa  revisao
//------------------------------------------------------------------
//
module unidade_controle (
    input clock,
    input reset,
    input iniciar,
    input fimT,
    input fimP,
    input nivel_concluido,
    input nivelIgualUltimoNivel,
    input nivelMenorOuIgualUltimoNivel,
    output reg ganhou,
    output reg passou_nivel,
    output reg zeraT,
    output reg contaT,
    output reg contaN,
    output reg zeraN,
    output reg contaP,
    output reg zeraP,
    output reg zeraM,
    output reg [4:0] db_estado
);

    // Define estados
    parameter inicial            = 5'b00000;  // 0
    parameter preparacao         = 5'b00001;  // 1
    parameter inic_nivel         = 5'b00010;  // 2
    parameter jogando            = 5'b00011;  // 3
    parameter inic_apagado       = 5'b00100;  // 4
    parameter mostra_apagado     = 5'b00101;  // 5 
    parameter inic_aceso         = 5'b00110;  // 6
    parameter mostra_aceso       = 5'b00111;  // 7
    parameter proxima_piscagem   = 5'b01000;  // 8
    parameter fim_animacao       = 5'b01001;  // 9
    parameter checa_ultimo_nivel = 5'b01010;  // 10
    parameter proximo_nivel      = 5'b01011;  // 11
    parameter est_ganhou         = 5'b01100;  // 12 


    // Variaveis de estado
    reg [4:0] Eatual, Eprox;

    // Memoria de estado
    always @(posedge clock or posedge reset) begin
        if (reset)
            Eatual <= inicial;
        else
            Eatual <= Eprox;
    end

    // Logica de proximo estado
    always @* begin
        case (Eatual)
            inicial:            Eprox = iniciar ? preparacao : inicial;
            preparacao:         Eprox = inic_nivel;
            inic_nivel:         Eprox = jogando;
            jogando:            Eprox = nivel_concluido ? inic_apagado : jogando;
            inic_apagado:       Eprox = mostra_apagado;
            mostra_apagado:     Eprox = fimT ? inic_aceso : mostra_apagado;
            inic_aceso:         Eprox = mostra_aceso;
            mostra_aceso:
            begin 
                if (fimT && fimP)
                    Eprox = fim_animacao;
                else if (fimT && !fimP)
                    Eprox = proxima_piscagem;
                else
                    Eprox = mostra_aceso;
            end
            proxima_piscagem:   Eprox = inic_apagado;
            fim_animacao:       Eprox = checa_ultimo_nivel;
            checa_ultimo_nivel: 
            begin 
                if (nivelIgualUltimoNivel)
                    Eprox =  est_ganhou;
                else 
                    Eprox = proximo_nivel;
            end
            proximo_nivel:      Eprox = inic_nivel;
            est_ganhou:         Eprox = iniciar ? preparacao : est_ganhou;
            default:            Eprox = inicial;
        endcase
    end

    // Logica de saida (maquina Moore)
    always @* begin
        // Inicializa todas as saídas com valores padrão
        contaN       = 1'b0;
        zeraN        = 1'b0;
        contaP       = 1'b0;
        zeraP        = 1'b0;
        contaT       = 1'b0;
        zeraT        = 1'b0;
        zeraM        = 1'b0;
        ganhou       = 1'b0;
        passou_nivel = 1'b0;

        // Define sinais de controle
        case (Eatual)
            inicial: begin
                zeraN = 1'b1;
                zeraM = 1'b1;
            end

            preparacao: begin
                zeraN = 1'b1;
                zeraM = 1'b1;
                zeraP = 1'b1;
                zeraT = 1'b1;
            end

            inic_nivel: begin
                zeraM = 1'b1;
            end

            inic_apagado: begin
                zeraT        = 1'b1;
                passou_nivel = 1'b0;
                zeraM        = 1'b1;
            end

            mostra_apagado: begin
                contaT = 1'b1;
                passou_nivel = 1'b0;
            end

            inic_aceso: begin
                zeraT        = 1'b1;
                passou_nivel = 1'b1;
                zeraM        = 1'b1;       
            end

            mostra_aceso: begin
                contaT       = 1'b1;
                passou_nivel = 1'b1;
            end

            proxima_piscagem: begin
                contaP = 1'b1;
            end

            fim_animacao: begin
                zeraP = 1'b1;
            end

            proximo_nivel: begin
                contaN       = 1'b1;
                passou_nivel = 1'b0;
            end

            est_ganhou: begin
                ganhou       = 1'b1;
                passou_nivel = 1'b1;
            end

            default: begin
                // Mantém os sinais padrão
            end
        endcase

        // Saida de depuracao (estado)
        case (Eatual)
            inicial:            db_estado = 5'b00000;  // 0 
            preparacao:         db_estado = 5'b00001;  // 1 
            inic_nivel:         db_estado = 5'b00010;  // 2 
            jogando:            db_estado = 5'b00011;  // 3 
            inic_apagado:       db_estado = 5'b00100;  // 4 
            mostra_apagado:     db_estado = 5'b00101;  // 5 
            inic_aceso:         db_estado = 5'b00110;  // 6 
            mostra_aceso:       db_estado = 5'b00111;  // 7 
            proxima_piscagem:   db_estado = 5'b01000;  // 8 
            fim_animacao:       db_estado = 5'b01001;  // 9 
            checa_ultimo_nivel: db_estado = 5'b01010;  // 10
            proximo_nivel:      db_estado = 5'b01011;  // 11
            est_ganhou:         db_estado = 5'b01100;  // 12  
            default:            db_estado = 5'b11111;  // E (erro)
        endcase
    end

endmodule


/* ----------------------------------------------------------------
 * Arquivo   : hexa7seg.v
 * Projeto   : Experiencia 2 - Um Fluxo de Dados Simples
 *--------------------------------------------------------------
 * Descricao : decodificador hexadecimal para 
 *             display de 7 segmentos 
 * 
 * entrada : hexa - codigo binario de 4 bits hexadecimal
 * saida   : sseg - codigo de 7 bits para display de 7 segmentos
 *
 * baseado no componente bcd7seg.v da Intel FPGA
 *--------------------------------------------------------------
 * dica de uso: mapeamento para displays da placa DE0-CV
 *              bit 6 mais significativo é o bit a esquerda
 *              p.ex. sseg(6) -> HEX0[6] ou HEX06
 *--------------------------------------------------------------
 * Revisoes  :
 *     Data        Versao  Autor             Descricao
 *     24/12/2023  1.0     Edson Midorikawa  criacao
 *--------------------------------------------------------------
 * /

module hexa7seg_ent3bit (hexa, display);
    input      [2:0] hexa;
    output reg [6:0] display;

    /*
     *    ---
     *   | 0 |
     * 5 |   | 1
     *   |   |
     *    ---
     *   | 6 |
     * 4 |   | 2
     *   |   |
     *    ---
     *     3
     * /
        
    always @(hexa)
    case (hexa)
        3'h0:    display = 7'b1000000;
        3'h1:    display = 7'b1111001;
        3'h2:    display = 7'b0100100;
        3'h3:    display = 7'b0110000;
        3'h4:    display = 7'b0011001;
        3'h5:    display = 7'b0010010;
        3'h6:    display = 7'b0000010;
        3'h7:    display = 7'b1111000;
        default: display = 7'b1111111;
    endcase
endmodule

/* ----------------------------------------------------------------
 * Arquivo   : hexa7seg.v
 * Projeto   : Experiencia 2 - Um Fluxo de Dados Simples
 *--------------------------------------------------------------
 * Descricao : decodificador hexadecimal para 
 *             display de 7 segmentos 
 * 
 * entrada : hexa - codigo binario de 4 bits hexadecimal
 * saida   : sseg - codigo de 7 bits para display de 7 segmentos
 *
 * baseado no componente bcd7seg.v da Intel FPGA
 *--------------------------------------------------------------
 * dica de uso: mapeamento para displays da placa DE0-CV
 *              bit 6 mais significativo é o bit a esquerda
 *              p.ex. sseg(6) -> HEX0[6] ou HEX06
 *--------------------------------------------------------------
 * Revisoes  :
 *     Data        Versao  Autor             Descricao
 *     24/12/2023  1.0     Edson Midorikawa  criacao
 *--------------------------------------------------------------
 * /

module hexa7seg_ent8bit (hexa, display);
    input      [7:0] hexa;
    output reg [6:0] display;

    /*
     *    ---
     *   | 0 |
     * 5 |   | 1
     *   |   |
     *    ---
     *   | 6 |
     * 4 |   | 2
     *   |   |
     *    ---
     *     3
     * /
        
    always @(hexa)
    case (hexa)
        8'b00000001:    display = 7'b1000000;
        8'b00000010:    display = 7'b1111001;
        8'b00000100:    display = 7'b0100100;
        8'b00001000:    display = 7'b0110000;
        8'b00010000:    display = 7'b0011001;
        8'b00100000:    display = 7'b0010010;
        8'b01000000:    display = 7'b0000010;
        8'b10000000:    display = 7'b1111000;
        default: display = 7'b1111111;
    endcase
endmodule

/* -----------------------------------------------------------------
 *  Arquivo   : comparador_85.v
 *  Projeto   : Experiencia 2 - Um Fluxo de Dados Simples
 * -----------------------------------------------------------------
 * Descricao : comparador de magnitude de 4 bits 
 *             similar ao CI 7485
 *             baseado em descricao comportamental disponivel em	
 * https://web.eecs.umich.edu/~jhayes/iscas.restore/74L85b.v
 * -----------------------------------------------------------------
 * Revisoes  :
 *     Data        Versao  Autor             Descricao
 *     21/12/2023  1.0     Edson Midorikawa  criacao
 * -----------------------------------------------------------------
 * /

module comparador_85 (ALBi, AGBi, AEBi, A, B, ALBo, AGBo, AEBo);

    input[2:0] A, B;
    input      ALBi, AGBi, AEBi;
    output     ALBo, AGBo, AEBo;
    wire[3:0]  CSL, CSG;

    assign CSL  = ~A + B + ALBi;
    assign ALBo = ~CSL[3];
    assign CSG  = A + ~B + AGBi;
    assign AGBo = ~CSG[3];
    assign AEBo = ((A == B) && AEBi);

endmodule /* comparador_85 * /

//------------------------------------------------------------------
// Arquivo   : contador_163.v
// Projeto   : Experiencia 2 - Um Fluxo de Dados Simples
//------------------------------------------------------------------
// Descricao : Contador binario de 4 bits, modulo 16
//             similar ao componente 74163
//
// baseado no componente Vrcntr4u.v do livro Digital Design Principles 
// and Practices, Fifth Edition, by John F. Wakerly              
//------------------------------------------------------------------
// Revisoes  :
//     Data        Versao  Autor             Descricao
//     14/12/2023  1.0     Edson Midorikawa  versao inicial
//------------------------------------------------------------------
//
module contador_163 ( clock, clr, ld, ent, enp, D, Q, rco );
    input clock, clr, ld, ent, enp;
    input [2:0] D;
    output reg [2:0] Q;
    output reg rco;

    always @ (posedge clock)
        if (~clr)               Q <= 3'd0;
        else if (~ld)           Q <= D;
        else if (ent && enp)    Q <= Q + 1'b1;
        else                    Q <= Q;
 
    always @ (Q or ent)
        if (ent && (Q == 3'd7))    rco = 1;
        else                       rco = 0;
endmodule

module edge_detector_global (
    input  clock,
    input  reset,
    input  [7:0] botoes,
    output reg [7:0] edge_detected
);

    reg [7:0] botoes_anterior;

    always @(posedge clock or posedge reset) begin
        if (reset) begin
            botoes_anterior <= 8'b00000000;  // Zera valores
            edge_detected   <= 8'b00000000;  // Zera saida
        end else begin
            edge_detected   <= (botoes & ~botoes_anterior); // Detecta borda de subida para todos os botões
            botoes_anterior <= botoes; // Atualiza o estado anterior
        end
    end
endmodule

/*
    Este módulo é o controlador de uma matriz de leds. Ele trata as linhas da matriz como terra e as 
    colunas como fase, logo, para ativar algo na linha 5, ele faz linhas = 01111 e ativa o que quiser
    nas colunas. 


* /

/*
    Este módulo é o controlador de uma matriz de leds. Ele trata as linhas da matriz como terra e as 
    colunas como fase, logo, para ativar algo na linha 5, ele faz linhas = 01111 e ativa o que quiser
    nas colunas. 


* /

module matriz_leds (
    input clk,              // Clock principal da FPGA
    input rst,              // Botão de reset
    input [7:0] botoes,     // Entrada dos botões físicos
    input [2:0] nivel,      // Nivel atual do jogador
    output reg nivel_concluido, // Output que avisa a UC se venceu
    output [7:0] colunas,   // Sinais para as colunas da matriz de LEDs
    output [7:0] linhas,    // Sinais para ativar linhas da matriz
    output [2:0] indice     // Sinais para indice dos vetores 
);

    reg [7:0] estado_leds [7:0]; // Matriz virtual para armazenar estado das LEDs
    reg [7:0] linha_atual;       // Variável para escanear as linhas
    reg [2:0] s_indice;
    integer i, j;

    initial begin
        for (i = 0; i < 8; i = i + 1) begin
            for (j = 0; j < 8; j = j + 1) begin
                    estado_leds[i][j] <= 0; // Desliga todas as LEDs
            end 
        end 
        linha_atual = 8'b00000001;
    end

    // Checa condição de vitória com base no nível atual
    always @(posedge clk or posedge rst) begin
        if (rst) begin
            nivel_concluido <= 0;
        end else begin
            case (nivel) 
                3'b000: nivel_concluido <= (estado_leds[0] == 8'b11111111);
                3'b001: nivel_concluido <= (estado_leds[0] == 8'b11111111) && (estado_leds[1] == 8'b11111111) && (estado_leds[2] == 8'b11111111);
                3'b010: nivel_concluido <= (estado_leds[0] == 8'b11111111) && (estado_leds[1] == 8'b11111111) && (estado_leds[2] == 8'b11111111) && (estado_leds[3] == 8'b11111111) && (estado_leds[4] == 8'b11111111);
                3'b011: nivel_concluido <= (estado_leds[0] == 8'b11111111) && (estado_leds[1] == 8'b11111111) && (estado_leds[2] == 8'b11111111) && (estado_leds[3] == 8'b11111111) && (estado_leds[4] == 8'b11111111) && (estado_leds[5] == 8'b11111111) && (estado_leds[6] == 8'b11111111);
                3'b100: nivel_concluido <= (estado_leds[0] == 8'b11111111) && (estado_leds[1] == 8'b11111111) && (estado_leds[2] == 8'b11111111) && (estado_leds[3] == 8'b11111111) && (estado_leds[4] == 8'b11111111) && (estado_leds[5] == 8'b11111111) && (estado_leds[6] == 8'b11111111) && (estado_leds[7] == 8'b11111111);
                default: nivel_concluido <= 0;
            endcase
        end
    end

    // Reset: Apaga todas as LEDs no início
    always @(posedge clk or posedge rst) begin
        i = 0;
        j = 0; 

        if (rst) begin
            for (i = 0; i < 8; i = i + 1) begin
                for (j = 0; j < 8; j = j + 1) begin
                    estado_leds[i][j] <= 0;       // Desliga todas as LEDs
                end 
            end 
        end else begin
            // Controle das LEDs pelos botões
            if (botoes[0]) begin 
                estado_leds[0][0] <= ~estado_leds[0][0];
                estado_leds[0][1] <= ~estado_leds[0][1];
                estado_leds[0][2] <= ~estado_leds[0][2];
                estado_leds[0][3] <= ~estado_leds[0][3];
                estado_leds[1][0] <= ~estado_leds[1][0];
                estado_leds[1][1] <= ~estado_leds[1][1];
                estado_leds[1][2] <= ~estado_leds[1][2];
                estado_leds[1][3] <= ~estado_leds[1][3];
                estado_leds[2][0] <= ~estado_leds[2][0];
                estado_leds[2][1] <= ~estado_leds[2][1];
                estado_leds[2][2] <= ~estado_leds[2][2];
                estado_leds[2][3] <= ~estado_leds[2][3];
                estado_leds[3][0] <= ~estado_leds[3][0];
                estado_leds[3][1] <= ~estado_leds[3][1];
                estado_leds[3][2] <= ~estado_leds[3][2];
                estado_leds[3][3] <= ~estado_leds[3][3];
                
            end 

            if (botoes[1]) begin
                estado_leds[0][4] <= ~estado_leds[0][4];
                estado_leds[1][4] <= ~estado_leds[1][4];
                estado_leds[2][4] <= ~estado_leds[2][4];
                estado_leds[3][4] <= ~estado_leds[3][4];
                estado_leds[0][5] <= ~estado_leds[0][5];
                estado_leds[1][5] <= ~estado_leds[1][5];
                estado_leds[2][5] <= ~estado_leds[2][5];
                estado_leds[3][5] <= ~estado_leds[3][5];
                estado_leds[0][6] <= ~estado_leds[0][6];
                estado_leds[1][6] <= ~estado_leds[1][6];
                estado_leds[2][6] <= ~estado_leds[2][6];
                estado_leds[3][6] <= ~estado_leds[3][6];
                estado_leds[0][7] <= ~estado_leds[0][7];
                estado_leds[1][7] <= ~estado_leds[1][7];
                estado_leds[2][7] <= ~estado_leds[2][7];
                estado_leds[3][7] <= ~estado_leds[3][7];
               
            end
            if (botoes[2]) begin
                estado_leds[4][0] <= ~estado_leds[4][0];
                estado_leds[5][0] <= ~estado_leds[5][0];
                estado_leds[6][0] <= ~estado_leds[6][0];
                estado_leds[7][0] <= ~estado_leds[7][0];
                estado_leds[4][1] <= ~estado_leds[4][1];
                estado_leds[5][1] <= ~estado_leds[5][1];
                estado_leds[6][1] <= ~estado_leds[6][1];
                estado_leds[7][1] <= ~estado_leds[7][1];
                estado_leds[4][2] <= ~estado_leds[4][2];
                estado_leds[5][2] <= ~estado_leds[5][2];
                estado_leds[6][2] <= ~estado_leds[6][2];
                estado_leds[7][2] <= ~estado_leds[7][2];
                estado_leds[4][3] <= ~estado_leds[4][3];
                estado_leds[5][3] <= ~estado_leds[5][3];
                estado_leds[6][3] <= ~estado_leds[6][3];
                estado_leds[7][3] <= ~estado_leds[7][3];
            end
        
            if (botoes[3]) begin
                estado_leds[4][4] <= ~estado_leds[4][4];
                estado_leds[5][4] <= ~estado_leds[5][4];
                estado_leds[6][4] <= ~estado_leds[6][4];
                estado_leds[7][4] <= ~estado_leds[7][4];
                estado_leds[4][5] <= ~estado_leds[4][5];
                estado_leds[5][5] <= ~estado_leds[5][5];
                estado_leds[6][5] <= ~estado_leds[6][5];
                estado_leds[7][5] <= ~estado_leds[7][5];
                estado_leds[4][6] <= ~estado_leds[4][6];
                estado_leds[5][6] <= ~estado_leds[5][6];
                estado_leds[6][6] <= ~estado_leds[6][6];
                estado_leds[7][6] <= ~estado_leds[7][6];
                estado_leds[4][7] <= ~estado_leds[4][7];
                estado_leds[5][7] <= ~estado_leds[5][7];
                estado_leds[6][7] <= ~estado_leds[6][7];
                estado_leds[7][7] <= ~estado_leds[7][7];
            end
            if (botoes[4]) begin
                estado_leds[2][2] <= ~estado_leds[2][2];
                estado_leds[3][2] <= ~estado_leds[3][2];
                estado_leds[4][2] <= ~estado_leds[4][2];
                estado_leds[5][2] <= ~estado_leds[5][2];
                estado_leds[2][3] <= ~estado_leds[2][3];
                estado_leds[3][3] <= ~estado_leds[3][3];
                estado_leds[4][3] <= ~estado_leds[4][3];
                estado_leds[5][3] <= ~estado_leds[5][3];
                estado_leds[2][4] <= ~estado_leds[2][4];
                estado_leds[3][4] <= ~estado_leds[3][4];
                estado_leds[4][4] <= ~estado_leds[4][4];
                estado_leds[5][4] <= ~estado_leds[5][4];
                estado_leds[2][5] <= ~estado_leds[2][5];
                estado_leds[3][5] <= ~estado_leds[3][5];
                estado_leds[4][5] <= ~estado_leds[4][5];
                estado_leds[5][5] <= ~estado_leds[5][5];
            end
            if (botoes[5]) begin
                estado_leds[0][0] <= ~estado_leds[0][0];
                estado_leds[0][1] <= ~estado_leds[0][1];
                estado_leds[0][2] <= ~estado_leds[0][2];
                estado_leds[0][3] <= ~estado_leds[0][3];
                estado_leds[0][4] <= ~estado_leds[0][4];
                estado_leds[0][5] <= ~estado_leds[0][5];
                estado_leds[0][6] <= ~estado_leds[0][6];
                estado_leds[0][7] <= ~estado_leds[0][7];
                estado_leds[2][0] <= ~estado_leds[2][0];
                estado_leds[2][1] <= ~estado_leds[2][1];
                estado_leds[2][2] <= ~estado_leds[2][2];
                estado_leds[2][3] <= ~estado_leds[2][3];
                estado_leds[2][4] <= ~estado_leds[2][4];
                estado_leds[2][5] <= ~estado_leds[2][5];
                estado_leds[2][6] <= ~estado_leds[2][6];
                estado_leds[2][7] <= ~estado_leds[2][7];
                estado_leds[4][0] <= ~estado_leds[4][0];
                estado_leds[4][1] <= ~estado_leds[4][1];
                estado_leds[4][2] <= ~estado_leds[4][2];
                estado_leds[4][3] <= ~estado_leds[4][3];
                estado_leds[4][4] <= ~estado_leds[4][4];
                estado_leds[4][5] <= ~estado_leds[4][5];
                estado_leds[4][6] <= ~estado_leds[4][6];
                estado_leds[4][7] <= ~estado_leds[4][7];
                estado_leds[6][0] <= ~estado_leds[6][0];
                estado_leds[6][1] <= ~estado_leds[6][1];
                estado_leds[6][2] <= ~estado_leds[6][2];
                estado_leds[6][3] <= ~estado_leds[6][3];
                estado_leds[6][4] <= ~estado_leds[6][4];
                estado_leds[6][5] <= ~estado_leds[6][5];
                estado_leds[6][6] <= ~estado_leds[6][6];
                estado_leds[6][7] <= ~estado_leds[6][7];
            end
            if (botoes[6]) begin
                estado_leds[0][0] <= ~estado_leds[0][0];
                estado_leds[1][0] <= ~estado_leds[1][0];
                estado_leds[2][0] <= ~estado_leds[2][0];
                estado_leds[3][0] <= ~estado_leds[3][0];
                estado_leds[4][0] <= ~estado_leds[4][0];
                estado_leds[5][0] <= ~estado_leds[5][0];
                estado_leds[6][0] <= ~estado_leds[6][0];
                estado_leds[7][0] <= ~estado_leds[7][0];
                estado_leds[0][2] <= ~estado_leds[0][2];
                estado_leds[1][2] <= ~estado_leds[1][2];
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*/
